# Fritzing sketch Layout (saved by Fritzing 0.9.3b)
breadboards: 1

parts:
  Bauteil1 = Arduino Nano (Rev3.0)
  RGB_SMD_LED1 = SMD RGB LED (WS2812) [package=5050]
  S1 = Taiway 100-SP-X-T1 SPDT Miniature Toggle Switch [part_number=100-SP-X-T1-0-0-B1-M2 package=THT]
  R1 = Resistor [tolerance=±5% resistance=220 package=THT]
  R2 = Resistor [tolerance=±5% resistance=220 package=THT]

nets:
  GND: Bauteil1.GND, RGB_SMD_LED1.VSS
  N1: Bauteil1.D2, R2.Pin_1
  N2: Bauteil1.D3, R1.Pin_1
  N3: Bauteil1.D4, RGB_SMD_LED1.DIn
  5V: Bauteil1.5V, RGB_SMD_LED1.VCC
  N4: S1.L1, R2.Pin_0
  N5: S1.L2, R1.Pin_0
